// Logisim project MiniMIPSLeah (1).circ as structural Verilog: 14 circuits, main circuit MIPS
module MIPS (
  output [31:0] out_1,
  output [4:0] out_2,
  output [31:0] res,
  output [4:0] destination
);

  wire clock_1_out, decodestage_1_islui, decodestage_1_isrtype, decodestage_1_issltorsltu,
       decodestage_1_isunsigned, decodestage_1_isvariableshift, decodestage_1_writeenable,
       execute_1_writeenout, exmem_1_writeenout, hazarddetect_1_mema, hazarddetect_1_memb,
       hazarddetect_1_wba, hazarddetect_1_wbb, idex_1_isrout, idex_1_isunsignedout, idex_1_luiout,
       idex_1_sltsltiuout, idex_1_variableshiftout, idex_1_writeenout, memory_1_writeenout,
       memwb_1_writeenout, not_1_out, registerfile_1_p3;
  wire [3:0] decodestage_1_aluop, idex_1_aluopout;
  wire [4:0] decodestage_1_dest, decodestage_1_ra, decodestage_1_rb, decodestage_1_sa, execute_1_destout,
       exmem_1_rdout, idex_1_raout, idex_1_rbout, idex_1_rdout, idex_1_saout, memory_1_dest, memwb_1_destout;
  wire [29:0] incrementer_1_p2;
  wire [31:0] decodestage_1_immediate, execute_1_bout, execute_1_c, exmem_1_bout, exmem_1_coutt, idex_1_aout,
       idex_1_bout, idex_1_immout, instruction_q, memory_1_boutt, memory_1_cout, memwb_1_boutt,
       memwb_1_coutt, mipsprogramrom_1_p2, multiplexer_1_out, multiplexer_2_out, multiplexer_3_out,
       multiplexer_4_out, register_1_q, registerfile_1_p7, registerfile_1_p8;

  Clock clock_1 (.out(clock_1_out));
  Register #(.width(32)) register_1 (
    .D({incrementer_1_p2, register_1_q[1:0]}), .clk(clock_1_out), .Q(register_1_q));  // open: en, clr
  // MIPSProgramROM mipsprogramrom_1: pin names not known; wires that end beside it: register_1_q, mipsprogramrom_1_p2
  // Incrementer #(.width(30)) incrementer_1: pin names not known; wires that end beside it: register_1_q[31:2], incrementer_1_p2
  Register #(.width(32)) instruction (.D(mipsprogramrom_1_p2), .clk(clock_1_out), .Q(instruction_q));  // open: en, clr
  not not_1 (not_1_out, clock_1_out);
  DecodeStage decodestage_1 (
    .instruction(instruction_q), .Dest(decodestage_1_dest), .rA(decodestage_1_ra), .rB(decodestage_1_rb),
    .Sa(decodestage_1_sa), .immediate(decodestage_1_immediate),
    .isVariableShift(decodestage_1_isvariableshift), .ALUOP(decodestage_1_aluop),
    .writeEnable(decodestage_1_writeenable), .isUnsigned(decodestage_1_isunsigned),
    .isSLTorSLTU(decodestage_1_issltorsltu), .isLUI(decodestage_1_islui), .isRType(decodestage_1_isrtype));
  // RegisterFile registerfile_1: pin names not known; wires that end beside it: out_1, not_1_out, registerfile_1_p3, destination, decodestage_1_ra, decodestage_1_rb, registerfile_1_p7, registerfile_1_p8
  IDEX idex_1 (
    .A(registerfile_1_p7), .B(registerfile_1_p8), .Ra(decodestage_1_ra), .Sa(decodestage_1_sa),
    .Rb(decodestage_1_rb), .Rd(decodestage_1_dest), .Immediate(decodestage_1_immediate),
    .isUnsigned(decodestage_1_isunsigned), .writeEnin(decodestage_1_writeenable),
    .ALUOp(decodestage_1_aluop), .isSLTorSLTU(decodestage_1_issltorsltu), .isLUI(decodestage_1_islui),
    .isRType(decodestage_1_isrtype), .isVariableShift(decodestage_1_isvariableshift), .clockin(clock_1_out),
    .Aout(idex_1_aout), .Bout(idex_1_bout), .RaOut(idex_1_raout), .SaOut(idex_1_saout), .RbOut(idex_1_rbout),
    .RdOut(idex_1_rdout), .ImmOut(idex_1_immout), .isUnsignedOut(idex_1_isunsignedout),
    .writeEnOut(idex_1_writeenout), .AluOpOut(idex_1_aluopout), .SltSLTiuOut(idex_1_sltsltiuout),
    .LUIOUT(idex_1_luiout), .isROut(idex_1_isrout), .variableShiftOut(idex_1_variableshiftout));
  Multiplexer #(.width(32), .enable("false")) multiplexer_1 (
    .in0(idex_1_bout), .in1(out_1), .out(multiplexer_1_out), .sel(hazarddetect_1_wbb));
  Multiplexer #(.width(32), .enable("false")) multiplexer_2 (
    .in0(idex_1_aout), .in1(out_1), .out(multiplexer_2_out), .sel(hazarddetect_1_wba));
  Multiplexer #(.width(32), .enable("false")) multiplexer_3 (
    .in0(multiplexer_1_out), .in1(exmem_1_coutt), .out(multiplexer_3_out), .sel(hazarddetect_1_memb));
  Execute execute_1 (
    .dest(idex_1_rdout), .A(multiplexer_4_out), .B(multiplexer_3_out), .immediate(idex_1_immout),
    .isSLTorSLTU(idex_1_sltsltiuout), .ALUOp(idex_1_aluopout), .isRType(idex_1_isrout),
    .isLUI(idex_1_luiout), .isUnsigned(idex_1_isunsignedout), .isVariableShift(idex_1_variableshiftout),
    .Sa(idex_1_saout), .writeEnable(idex_1_writeenout), .destout(execute_1_destout), .C(execute_1_c),
    .Bout(execute_1_bout), .writeEnOut(execute_1_writeenout));
  Multiplexer #(.width(32), .enable("false")) multiplexer_4 (
    .in0(multiplexer_2_out), .in1(exmem_1_coutt), .out(multiplexer_4_out), .sel(hazarddetect_1_mema));
  ExMem exmem_1 (
    .Rdin(execute_1_destout), .Bin(execute_1_bout), .Cin(execute_1_c), .writeEnIn(execute_1_writeenout),
    .clockIn(clock_1_out), .RdOut(exmem_1_rdout), .BOut(exmem_1_bout), .Coutt(exmem_1_coutt),
    .writeEnOut(exmem_1_writeenout));
  HazardDetect hazarddetect_1 (
    .MemWbRd(memwb_1_destout), .RaDecEx(idex_1_raout), .RbDecEx(idex_1_rbout), .RdExMem(exmem_1_rdout),
    .WBA(hazarddetect_1_wba), .MEMA(hazarddetect_1_mema), .WBB(hazarddetect_1_wbb), .MEMB(hazarddetect_1_memb));
  Memory memory_1 (
    .destout(exmem_1_rdout), .C(exmem_1_coutt), .Bout(exmem_1_bout), .writeEnIn(exmem_1_writeenout),
    .dest(memory_1_dest), .Cout(memory_1_cout), .Boutt(memory_1_boutt), .writeEnOut(memory_1_writeenout));
  MemWB memwb_1 (
    .Dest(memory_1_dest), .Cout(memory_1_cout), .Bout(memory_1_boutt), .writeEnIn(memory_1_writeenout),
    .clockin(clock_1_out), .Destout(memwb_1_destout), .Coutt(memwb_1_coutt), .Boutt(memwb_1_boutt),
    .writeEnOut(memwb_1_writeenout));
  writeBack writeback_1 (
    .C(memwb_1_coutt), .dest(memwb_1_destout), .B(memwb_1_boutt), .writeEnIn(memwb_1_writeenout),
    .writeResult(out_1), .destin(destination), .writeEnOut(registerfile_1_p3));

  assign out_2 = destination;
  assign res = out_1;

  // Notes on the sheet:
  //   contents of mipsprogramrom_1 (hex, n*v repeats v):
  //   #Max Chu mmc278 #testing for 3410 Mini Mips  #First two block will test everything from Table A
  //   #test WB and Mem Forwarding ADDIU $1, $1, 1 ADDIU $1, $1, 1 ADDIU $1, $1, 1 ADDIU $1, $1, 1 ADDIU
  //   $1, $1, 1 ADDIU $1, $1, 1 #register 1 should be 6  #clear ADDIU $1, $zero, 0 #register 1 should be 0
  //   #testing WB and Mem Forwarding for other instructions ADDIU $1, $1, 16 #1 should be 16 LUI $2, 1
  //   #testing LUI, should be 2^16 = 65536 ADDU $3, $1, $2 #WB forwarding and MEM forwarding, $3 should be
  //   65536 + 16 ORI $4, $3, 0 #should just copy over whatever is in register 3 ANDI $5, $3, 0 #should be
  //   all zero XORI $6, $5, 65535 #should be all ones SLT $7, $6, $5 #should be zero SLT $8, $5, $6
  //   #should be one SLTU $9, $6, $5 #should be zero SLTU $10, $5, $6 #should be one SLTI $11, $10, 0
  //   #should be zero SLTIU $12, $0, 10 #should be one AND $13, $zero, $11 #should be zero AND $14, $7,
  //   $10 #should be zero OR $15, $14, $10 #should be one OR $16, $13, $11 #should be zero XOR $17, $14,
  //   $15 #should be one L1: XOR $18, $17, $15 #should be zero NOR $19, $14, $10 #should be zero padded by
  //   ones NOR $20, $13, $11 #should be all ones MOVZ $21, $17, $18 #if B is equal to zero, then write A
  //   to B, should be one MOVZ $22, $21, $21 #should not do anything, so should stay zero  MOVN $23, $20,
  //   $17 #should be all ones MOVN $24, $20, $18 #should not do anything SLL $25, $20, 5 #should be 5 0's
  //   at beginning SRL $26, $20, 0 #should stay all ones SRA $27, $19, 5 #should be all 1's SRA $31, $20,
  //   5 #should stay all ones SLLV $28, $16, $15 #should be zero SRLV $29, $16, $15 #should be all zeros
  //   SRAV $30, $17, $19 #should be all zeros ADDU $30, $zero, $27 #loading all ones into 30 for more SRAV
  //   testing SRAV $31, $30, $6 #should stay all ones SRLV $31, $30, $31 #should be just one one J L1 JR
  //   $31 JAL L1 JALR $31, $2 BEQ $18, $18, L1 BNE $18, $15, L1 BLEZ $18, L1 BGTZ $18, L1 BGEZ $18, L1 LW
  //   $3, 0x0($8)  SW $3, 0x0($8) #// LB $3, 0x0($8) #// LBU $3, 0x0($8) #// SB $3, 0x0($8) #//
  //   memory mux
endmodule

module DecodeStage (
  input  [31:0] instruction,
  output [4:0] Dest,
  output [4:0] rA,
  output [4:0] rB,
  output [4:0] Sa,
  output [31:0] immediate,
  output isVariableShift,
  output [3:0] ALUOP,
  output writeEnable,
  output isUnsigned,
  output isSLTorSLTU,
  output isLUI,
  output isRType
);

  wire [31:0] bit_extender_1_out, bit_extender_2_out;

  nor nor_1 (isRType, instruction[26], instruction[27], instruction[28], instruction[29], instruction[30], instruction[31]);
  Multiplexer #(.width(5), .enable("false")) multiplexer_1 (
    .in0(instruction[20:16]), .in1(instruction[15:11]), .out(Dest), .sel(isRType));
  decodeALU decodealu_1 (
    .Func(instruction[5:0]), .isRType(isRType), .Op(instruction[31:26]), .isVariableShift(isVariableShift),
    .ALUOp(ALUOP), .writeEnable(writeEnable), .isUnsigned(isUnsigned), .isSLTorSLTU(isSLTorSLTU),
    .isLUI(isLUI));
  assign bit_extender_1_out = {{16{instruction[15]}}, instruction[15:0]};  // Bit_Extender bit_extender_1
  Multiplexer #(.width(32), .enable("false")) multiplexer_2 (
    .in0(bit_extender_1_out), .in1(bit_extender_2_out), .out(immediate), .sel(instruction[28]));
  assign bit_extender_2_out = {{16{1'b0}}, instruction[15:0]};  // Bit_Extender bit_extender_2

  assign rA = instruction[25:21];
  assign rB = instruction[20:16];
  assign Sa = instruction[10:6];
endmodule

module decodeALU (
  input  [5:0] Func,
  input  isRType,
  input  [5:0] Op,
  output isVariableShift,
  output [3:0] ALUOp,
  output writeEnable,
  output isUnsigned,
  output isSLTorSLTU,
  output isLUI
);

  wire and_1_out, and_2_out, and_5_out, and_6_out, nand_1_out, not_1_out, not_2_out, not_5_out, not_7_out,
       not_8_out;
  wire [0:0] not_4_out;
  wire [1:1] not_3_out;
  wire [3:0] multiplexer_1_out, multiplexer_2_out, multiplexer_3_out, multiplexer_4_out, multiplexer_5_out,
       multiplexer_6_out;
  wire [3:3] not_6_out;

  not not_1 (not_1_out, Op[2]);
  not not_2 (not_2_out, isRType);
  and and_1 (and_1_out, Func[1], isRType, Func[3]);
  and and_2 (and_2_out, Op[1], not_2_out, not_1_out);
  or or_1 (isUnsigned, Func[0], Op[0]);
  or or_2 (isSLTorSLTU, and_1_out, and_2_out);
  not not_3 (not_3_out[1], isRType);
  not not_4 (not_4_out[0], Func[2]);
  Multiplexer #(.width(4), .enable("false")) multiplexer_1 (
    .in0({Func[2:0], Func[3]}), .in1({Func[2:0], not_4_out[0]}), .out(multiplexer_1_out), .sel(Func[2]));
  and and_3 (isVariableShift, Func[2], not_5_out);
  not not_5 (not_5_out, Func[5]);
  Multiplexer #(.width(4), .enable("false")) multiplexer_2 (
    .in0({Op[2:0], Op[1]}), .in1({Op[2:0], isRType}), .out(multiplexer_2_out), .sel(Op[2]));
  not not_6 (not_6_out[3], isLUI);
  and and_4 (isLUI, Op[0], Op[1], Op[2], Op[3]);
  Multiplexer #(.width(4), .enable("false")) multiplexer_3 (
    .in0({Func[5], Func[1], not_3_out[1], Func[0]}), .in1(multiplexer_1_out), .out(multiplexer_3_out),
    .sel(Func[5]));
  Multiplexer #(.width(4), .enable("false")) multiplexer_4 (
    .in0({4{not_6_out[3]}}), .in1(multiplexer_5_out), .out(multiplexer_4_out), .sel(Op[3]));
  Multiplexer #(.width(4), .enable("false")) multiplexer_5 (
    .in0(multiplexer_2_out), .in1({4{not_6_out[3]}}), .out(multiplexer_5_out), .sel(isLUI));
  Multiplexer #(.width(4), .enable("false")) multiplexer_6 (
    .in0(multiplexer_4_out), .in1(multiplexer_3_out), .out(multiplexer_6_out), .sel(isRType));
  Multiplexer #(.width(4), .enable("false")) multiplexer_7 (
    .in0(multiplexer_6_out), .in1({4{not_6_out[3]}}), .out(ALUOp), .sel(Op[5]));
  not not_7 (not_7_out, Func[5]);
  nand nand_1 (nand_1_out, not_7_out, Func[3]);
  not not_8 (not_8_out, Op[5]);
  and and_5 (and_5_out, not_8_out, Op[3]);
  and and_6 (and_6_out, isRType, nand_1_out);
  or or_3 (writeEnable, and_6_out, and_5_out);

  // Notes on the sheet:
  //   1 if ANDORXORNOR, 0 if else
  //   1 if SLTIU, 0 if ADDIU
  //   1 if ANDIORIXORI, 0 if ow
  //   0 if ADDU/SUBU, 1 if SLTU
  //   0 if shift, 1 if not
  //   1 if IType, 0 if JType
  //   is Rtype or Not
  //   isLoadStore
  //   DELETE THIS WHEN MAKING JUMPS
  //   1 if LUI, 0 if not
endmodule

module ShiftSixteen (
  input  [15:0] firstSixteen,
  output [31:0] LUId
);

  wire not_1_out;

  not not_1 (not_1_out, firstSixteen[0]);
  and and_1 (LUId[15], firstSixteen[0], not_1_out);

  assign {LUId[31:16], LUId[14:0]} = {firstSixteen, {15{LUId[15]}}};
endmodule

module Execute (
  input  [4:0] dest,
  input  [31:0] A,
  input  [31:0] B,
  input  [31:0] immediate,
  input  isSLTorSLTU,
  input  [3:0] ALUOp,
  input  isRType,
  input  isLUI,
  input  isUnsigned,
  input  isVariableShift,
  input  [4:0] Sa,
  input  writeEnable,
  output [4:0] destout,
  output [31:0] C,
  output [31:0] Bout,
  output writeEnOut
);

  wire and_1_out, and_2_out, comparator_1_lt, comparator_2_lt, iszero_1_iszero, not_1_out, not_2_out,
       not_3_out;
  wire [4:0] multiplexer_1_out;
  wire [4:4] xor_1_out;
  wire [31:0] bit_extender_1_out, bit_extender_2_out, mips_alu_1_p5, multiplexer_2_out, multiplexer_3_out,
       multiplexer_4_out, multiplexer_5_out, multiplexer_6_out, multiplexer_7_out, shiftsixteen_1_luid;

  Multiplexer #(.width(5), .enable("false")) multiplexer_1 (
    .in0(Sa), .in1(A[4:0]), .out(multiplexer_1_out), .sel(isVariableShift));
  Multiplexer #(.width(32), .enable("false")) multiplexer_2 (
    .in0(B), .in1(immediate), .out(multiplexer_2_out), .sel(not_1_out));
  Multiplexer #(.width(32), .enable("false")) multiplexer_3 (
    .in0(B), .in1(immediate), .out(multiplexer_3_out), .sel(not_1_out));
  not not_1 (not_1_out, isRType);
  Comparator #(.width(32)) comparator_1 (.a(A), .b(multiplexer_2_out), .lt(comparator_1_lt));  // open: gt, eq
  Comparator #(.width(32), .mode("unsigned")) comparator_2 (
    .a(A), .b(multiplexer_2_out), .lt(comparator_2_lt));  // open: gt, eq
  not not_2 (not_2_out, immediate[5]);
  // Mips_ALU mips_alu_1: pin names not known; wires that end beside it: A, multiplexer_3_out, ALUOp, multiplexer_1_out, mips_alu_1_p5
  assign bit_extender_1_out = {{31{1'b0}}, comparator_1_lt};  // Bit_Extender bit_extender_1
  assign bit_extender_2_out = {{31{1'b0}}, comparator_2_lt};  // Bit_Extender bit_extender_2
  and and_1 (and_1_out, isRType, immediate[3], not_2_out);
  Multiplexer #(.width(32), .enable("false")) multiplexer_4 (
    .in0(bit_extender_1_out), .in1(bit_extender_2_out), .out(multiplexer_4_out), .sel(isUnsigned));
  ShiftSixteen shiftsixteen_1 (.firstSixteen(immediate[15:0]), .LUId(shiftsixteen_1_luid));
  isZero iszero_1 (.B(B), .isZero(iszero_1_iszero));
  not not_3 (not_3_out, xor_1_out[4]);
  Multiplexer #(.width(32), .enable("false")) multiplexer_5 (
    .in0(mips_alu_1_p5), .in1(multiplexer_4_out), .out(multiplexer_5_out), .sel(isSLTorSLTU));
  and and_2 (and_2_out, not_3_out, and_1_out);
  Multiplexer #(.width(32), .enable("false")) multiplexer_6 (
    .in0(multiplexer_5_out), .in1(multiplexer_7_out), .out(multiplexer_6_out), .sel(and_1_out));
  Multiplexer #(.width(32), .enable("false")) multiplexer_7 (
    .in0(multiplexer_5_out), .in1(A), .out(multiplexer_7_out), .sel(xor_1_out[4]));
  xor xor_1 (xor_1_out[4], iszero_1_iszero, immediate[0]);
  Multiplexer #(.width(5), .enable("false")) multiplexer_8 (
    .in0(dest), .in1({5{xor_1_out[4]}}), .out(destout), .sel(and_2_out));
  Multiplexer #(.width(32), .enable("false")) multiplexer_9 (
    .in0(multiplexer_6_out), .in1(shiftsixteen_1_luid), .out(C), .sel(isLUI));

  assign Bout = B;
  assign writeEnOut = writeEnable;

  // Notes on the sheet:
  //   signed comparator
  //   unsigned comp
  //   Is is SLT or SLTU?
  //   Did the move output a 1?
  //   MOVZ or MOVN?
  //   Is it a move?
endmodule

module Memory (
  input  [4:0] destout,
  input  [31:0] C,
  input  [31:0] Bout,
  input  writeEnIn,
  output [4:0] dest,
  output [31:0] Cout,
  output [31:0] Boutt,
  output writeEnOut
);


  assign Boutt = Bout;
  assign Cout = C;
  assign dest = destout;
  assign writeEnOut = writeEnIn;
endmodule

module writeBack (
  input  [31:0] C,
  input  [4:0] dest,
  input  [31:0] B,
  input  writeEnIn,
  output [31:0] writeResult,
  output [4:0] destin,
  output writeEnOut
);


  assign destin = dest;
  assign writeEnOut = writeEnIn;
  assign writeResult = C;
endmodule

module isZero (
  input  [31:0] B,
  output isZero
);

  wire or_1_out;

  or or_1 (or_1_out, B[0], B[1], B[2], B[3], B[4], B[5], B[6], B[7], B[8], B[9], B[10], B[11], B[12], B[13], B[14], B[15], B[16], B[17], B[18], B[19], B[20], B[21], B[22], B[23], B[24], B[25], B[26], B[27], B[28], B[29], B[30], B[31]);
  not not_1 (isZero, or_1_out);
endmodule

module HazardDetect (
  input  [4:0] MemWbRd,
  input  [4:0] RaDecEx,
  input  [4:0] RbDecEx,
  input  [4:0] RdExMem,
  output WBA,
  output MEMA,
  output WBB,
  output MEMB
);

  wire equals5bit_1_iseq, equals5bit_2_iseq, equals5bit_3_iseq, equals5bit_4_iseq, notzero5bit_1_isnotzero,
       notzero5bit_2_p2, notzero5bit_3_isnotzero, notzero5bit_4_isnotzero;

  notZero5Bit notzero5bit_1 (.A(MemWbRd), .isNotZero(notzero5bit_1_isnotzero));
  equals5bit equals5bit_1 (.A(MemWbRd), .B(RaDecEx), .isEq(equals5bit_1_iseq));
  // notZero5Bit notzero5bit_2: pin names not known; wires that end beside it: MemWbRd, notzero5bit_2_p2
  equals5bit equals5bit_2 (.A(MemWbRd), .B(RbDecEx), .isEq(equals5bit_2_iseq));
  and and_1 (WBA, notzero5bit_1_isnotzero, equals5bit_1_iseq);
  and and_2 (WBB, notzero5bit_2_p2, equals5bit_2_iseq);
  notZero5Bit notzero5bit_3 (.A(RdExMem), .isNotZero(notzero5bit_3_isnotzero));
  equals5bit equals5bit_3 (.A(RdExMem), .B(RaDecEx), .isEq(equals5bit_3_iseq));
  notZero5Bit notzero5bit_4 (.A(RdExMem), .isNotZero(notzero5bit_4_isnotzero));
  equals5bit equals5bit_4 (.A(RdExMem), .B(RbDecEx), .isEq(equals5bit_4_iseq));
  and and_3 (MEMA, notzero5bit_3_isnotzero, equals5bit_3_iseq);
  and and_4 (MEMB, notzero5bit_4_isnotzero, equals5bit_4_iseq);

  // Notes on the sheet:
  //   Forward A
  //   Forward B
endmodule

module equals5bit (
  input  [4:0] A,
  input  [4:0] B,
  output isEq
);

  wire [4:0] xnor_1_out;

  assign xnor_1_out = ~(A ^ B);  // XNOR_Gate xnor_1, 5 bits wide
  and and_1 (isEq, xnor_1_out[0], xnor_1_out[1], xnor_1_out[2], xnor_1_out[3], xnor_1_out[4]);
endmodule

module notZero5Bit (
  input  [4:0] A,
  output isNotZero
);

  or or_1 (isNotZero, A[0], A[1], A[2], A[3], A[4]);
endmodule

module IDEX (
  input  [31:0] A,
  input  [31:0] B,
  input  [4:0] Ra,
  input  [4:0] Sa,
  input  [4:0] Rb,
  input  [4:0] Rd,
  input  [31:0] Immediate,
  input  isUnsigned,
  input  writeEnin,
  input  [3:0] ALUOp,
  input  isSLTorSLTU,
  input  isLUI,
  input  isRType,
  input  isVariableShift,
  input  clockin,
  output [31:0] Aout,
  output [31:0] Bout,
  output [4:0] RaOut,
  output [4:0] SaOut,
  output [4:0] RbOut,
  output [4:0] RdOut,
  output [31:0] ImmOut,
  output isUnsignedOut,
  output writeEnOut,
  output [3:0] AluOpOut,
  output SltSLTiuOut,
  output LUIOUT,
  output isROut,
  output variableShiftOut
);

  Register #(.width(5)) register_1 (.D(Ra), .clk(clockin), .Q(RaOut));  // open: en, clr
  Register #(.width(5)) register_2 (.D(Rb), .clk(clockin), .Q(RbOut));  // open: en, clr
  Register #(.width(1)) register_3 (.D(writeEnin), .clk(clockin), .Q(writeEnOut));  // open: en, clr
  Register #(.width(32)) register_4 (.D(A), .clk(clockin), .Q(Aout));  // open: en, clr
  Register #(.width(32)) register_5 (.D(B), .clk(clockin), .Q(Bout));  // open: en, clr
  Register #(.width(5)) register_6 (.D(Sa), .clk(clockin), .Q(SaOut));  // open: en, clr
  Register #(.width(5)) register_7 (.D(Rd), .clk(clockin), .Q(RdOut));  // open: en, clr
  Register #(.width(32)) register_8 (.D(Immediate), .clk(clockin), .Q(ImmOut));  // open: en, clr
  Register #(.width(1)) register_9 (.D(isUnsigned), .clk(clockin), .Q(isUnsignedOut));  // open: en, clr
  Register #(.width(4)) register_10 (.D(ALUOp), .clk(clockin), .Q(AluOpOut));  // open: en, clr
  Register #(.width(1)) register_11 (.D(isSLTorSLTU), .clk(clockin), .Q(SltSLTiuOut));  // open: en, clr
  Register #(.width(1)) register_12 (.D(isLUI), .clk(clockin), .Q(LUIOUT));  // open: en, clr
  Register #(.width(1)) register_13 (.D(isRType), .clk(clockin), .Q(isROut));  // open: en, clr
  Register #(.width(1)) register_14 (.D(isVariableShift), .clk(clockin), .Q(variableShiftOut));  // open: en, clr
endmodule

module ExMem (
  input  [4:0] Rdin,
  input  [31:0] Bin,
  input  [31:0] Cin,
  input  writeEnIn,
  input  clockIn,
  output [4:0] RdOut,
  output [31:0] BOut,
  output [31:0] Coutt,
  output writeEnOut
);

  Register #(.width(5)) Rd (.D(Rdin), .clk(clockIn), .Q(RdOut));  // open: en, clr
  Register #(.width(32)) B (.D(Bin), .clk(clockIn), .Q(BOut));  // open: en, clr
  Register #(.width(32)) Cout (.D(Cin), .clk(clockIn), .Q(Coutt));  // open: en, clr
  Register #(.width(1)) register_1 (.D(writeEnIn), .clk(clockIn), .Q(writeEnOut));  // open: en, clr
endmodule

module MemWB (
  input  [4:0] Dest,
  input  [31:0] Cout,
  input  [31:0] Bout,
  input  writeEnIn,
  input  clockin,
  output [4:0] Destout,
  output [31:0] Coutt,
  output [31:0] Boutt,
  output writeEnOut
);

  Register #(.width(5)) register_1 (.D(Dest), .clk(clockin), .Q(Destout));  // open: en, clr
  Register #(.width(32)) register_2 (.D(Cout), .clk(clockin), .Q(Coutt));  // open: en, clr
  Register #(.width(32)) register_3 (.D(Bout), .clk(clockin), .Q(Boutt));  // open: en, clr
  Register #(.width(1)) register_4 (.D(writeEnIn), .clk(clockin), .Q(writeEnOut));  // open: en, clr
endmodule
